// Logisim project Computador.circ as structural Verilog: 8 circuits, main circuit main
module PC (
  input  Load,
  input  Pause,
  input  [15:0] ADDRESS,
  input  Clock,
  input  enable,
  input  Reset,
  output [15:0] Q
);

  wire and_1_out, not_1_out, not_2_out;
  wire [15:0] adder_1_out, bitselector_1_out, multiplexer_1_out, multiplexer_2_out;

  not not_1 (not_1_out, Load);
  not not_2 (not_2_out, Pause);
  Multiplexer #(.width(16)) multiplexer_1 (.in1(adder_1_out), .out(multiplexer_1_out), .sel(not_1_out));  // open: in0
  and and_1 (and_1_out, not_2_out, Clock);
  Multiplexer #(.width(16)) multiplexer_2 (.in0(multiplexer_1_out), .in1(ADDRESS), .out(multiplexer_2_out), .sel(Load));
  Register #(.width(16)) register_1 (.D(multiplexer_2_out), .en(enable), .clk(and_1_out), .Q(Q), .clr(Reset));
  BitSelector #(.group(16), .width(1)) bitselector_1 (.in(enable), .out(bitselector_1_out), .sel(and_1_out));
  Adder #(.width(16)) adder_1 (.a(Q), .b(bitselector_1_out), .out(adder_1_out));  // open: cin, cout

  // Notes on the sheet:
  //   enable: pull=up
endmodule

module main (
  input  Clk2pulsos,
  input  En,
  input  Reset,
  input  Clk1pulso,
  input  [15:0] DataMemRead,
  output Write,
  output [7:0] INSTRUCTION,
  output [15:0] DataMem,
  output [15:0] Address,
  output [6:0] ASCIIDATA,
  output clkTTY
);

  wire alu_1_storeres, and_1_out, and_2_out, and_3_out, asciidecoder_1_back, asciidecoder_1_nextchar,
       asciidecoder_1_pausepc, demultiplexer_1_out0, demultiplexer_1_out1, demultiplexer_1_out2,
       demultiplexer_1_out3, demultiplexer_1_out4, demultiplexer_1_out5, demultiplexer_1_out6,
       demultiplexer_1_out7, EN_ALU, EN_ALU16, multiplexer_1_out, multiplexer_4_out, multiplexer_5_out,
       Nclk2, NClock, or_1_out, or_2_out, regarray_1_alusignal, regarray_1_en_acc, regarray_1_enabledecoder,
       regarray_1_sign;
  wire [1:0] dec_1_op;
  wire [2:0] dec_1_destiny, dec_1_from, OP;
  wire [3:0] FLAG, regarray_1_asciiformat;
  wire [7:0] bit_extender_1_out, dec_1_data;
  wire [15:0] ACC, B, multiplexer_2_out, multiplexer_3_out, regarray_1_to_acc, regarray_1_to_alu, result;

  and and_1 (and_1_out, Clk2pulsos, Clk1pulso);
  Multiplexer multiplexer_1 (.in0(NClock), .in1(and_1_out), .out(multiplexer_1_out), .sel(EN_ALU16));
  ALU alu_1 (
    .Enable(EN_ALU), .Operation(OP), .sub(regarray_1_alusignal), .ACC(B), .Data(ACC), .RESET(Reset),
    .clk(multiplexer_1_out), .S(result), .Flag_out(FLAG), .StoreRes(alu_1_storeres));  // open: Zero, Sign, greater, overflow, out_8
  not not_1 (NClock, Clk2pulsos);
  not not_2 (Nclk2, Clk1pulso);
  LED overflow (.in(FLAG[3]));
  LED greater (.in(FLAG[2]));
  LED s (.in(FLAG[1]));
  LED z (.in(FLAG[0]));
  Demultiplexer #(.select(3)) demultiplexer_1 (
    .out0(demultiplexer_1_out0), .out1(demultiplexer_1_out1), .out2(demultiplexer_1_out2),
    .out3(demultiplexer_1_out3), .out4(demultiplexer_1_out4), .out5(demultiplexer_1_out5),
    .out6(demultiplexer_1_out6), .out7(demultiplexer_1_out7), .in(EN_ALU), .sel(OP));
  LED ADDSUB (.in(demultiplexer_1_out0));
  LED MULT (.in(demultiplexer_1_out1));
  LED OPA (.in(demultiplexer_1_out2));
  LED DIV (.in(demultiplexer_1_out3));
  LED ANA (.in(demultiplexer_1_out4));
  LED XRA (.in(demultiplexer_1_out5));
  LED ORA (.in(demultiplexer_1_out6));
  LED MODA (.in(demultiplexer_1_out7));
  DEC dec_1 (.in_1(DataMemRead), .DATA(dec_1_data), .FROM(dec_1_from), .DESTINY(dec_1_destiny), .OP(dec_1_op));
  Bit_Extender #(.in_width(16), .out_width(8)) bit_extender_1 (.in(ACC), .out(bit_extender_1_out));
  RegArray regarray_1 (
    .Ck(Clk2pulsos), .Nclock(NClock), .clk2(Clk1pulso), .Back(asciidecoder_1_back), .NCLK2(Nclk2),
    .PausePC(asciidecoder_1_pausepc), .NextChar(asciidecoder_1_nextchar), .res16bits(multiplexer_2_out),
    .ALUregister(result), .Op(dec_1_op), .Destin_OP(dec_1_destiny), .From(dec_1_from), .Cond(FLAG), .EN(En),
    .Acc_data(bit_extender_1_out), .RE(Reset), .Data(dec_1_data), .EnableDecoder(regarray_1_enabledecoder),
    .ASCIIFormat(regarray_1_asciiformat), .Sign(regarray_1_sign), .write(Write), .ADDRESS_BUS(Address),
    .ALU_OP(OP), .to_memory(DataMem), .TO_ALU(regarray_1_to_alu), .Enable_ALU(EN_ALU), .ALU16bit(EN_ALU16),
    .TO_ACC(regarray_1_to_acc), .en_ACC(regarray_1_en_acc), .INSTRUCTION(INSTRUCTION),
    .AluSignal(regarray_1_alusignal));  // open: StoreFormat, visuAdd, SP
  J_K_Flip_Flop j_k_ff_1 ();  // open: J, clk, K, Q, Qn, preset, reset
  Multiplexer #(.width(16)) multiplexer_2 (.in0(ACC), .in1(result), .out(multiplexer_2_out), .sel(EN_ALU16));
  TTY tty_1 (.data(ASCIIDATA), .clk(clkTTY), .we(clkTTY), .clr(Reset));
  Multiplexer #(.width(16)) multiplexer_3 (
    .in0(regarray_1_to_acc), .in1(result), .out(multiplexer_3_out), .sel(alu_1_storeres));
  or or_1 (or_1_out, alu_1_storeres, EN_ALU16, regarray_1_en_acc);
  Register #(.width(16)) u_acc (.D(multiplexer_3_out), .en(or_1_out), .Q(ACC), .clk(multiplexer_4_out), .clr(Reset));
  Multiplexer multiplexer_4 (.in0(and_2_out), .in1(Nclk2), .out(multiplexer_4_out), .sel(regarray_1_en_acc));
  and and_2 (and_2_out, or_2_out, Clk1pulso);
  or or_2 (or_2_out, regarray_1_en_acc, EN_ALU, alu_1_storeres);
  ASCIIDECODER asciidecoder_1 (
    .Nclk2tiks(Nclk2), .EnableOut(regarray_1_enabledecoder), .clk2tiks(Clk1pulso), .NormalClock(Clk2pulsos),
    .Data(DataMemRead), .format(regarray_1_asciiformat), .Sign(regarray_1_sign), .ASCIID(ASCIIDATA),
    .PausePC(asciidecoder_1_pausepc), .nextChar(asciidecoder_1_nextchar), .ClkToOUT(clkTTY),
    .Back(asciidecoder_1_back));  // open: D1unit, D2Ten, D3Hundred, D4Thousand, D5TenThousand
  Register #(.width(16)) ALU_B (.D(regarray_1_to_alu), .en(En), .Q(B), .clk(multiplexer_5_out), .clr(Reset));
  Multiplexer multiplexer_5 (.in0(and_3_out), .in1(NClock), .out(multiplexer_5_out), .sel(EN_ALU16));
  and and_3 (and_3_out, EN_ALU, Clk1pulso);

  // Other names for the same wires on the sheet: ASCII[6:0] = ASCIIDATA; Clk = Clk2pulsos; clk2 = Clk1pulso;
  //   ClockForTTY = clkTTY; data_to_mem8x16[15:0] = DataMem; Enable = En; OutData[15:0] = DataMemRead
endmodule

module CPU (
  input  Interrupt
);

  wire and_1_out, and_2_out, clock_1_out, clock_2_out, j_k_ff_1_q, j_k_ff_1_qn, main_1_clktty, main_1_write,
       not_1_out, turn_off_out, turn_on_out;
  wire [6:0] main_1_asciidata;
  wire [15:0] main_1_address, main_1_datamem, ram_1_dout;

  Button turn_on (.out(turn_on_out));
  Button turn_off (.out(turn_off_out));
  Clock #(.highDuration(2), .lowDuration(2)) clock_1 (.out(clock_1_out));
  Clock clock_2 (.out(clock_2_out));
  J_K_Flip_Flop j_k_ff_1 (
    .J(turn_on_out), .Q(j_k_ff_1_q), .Qn(j_k_ff_1_qn), .preset(turn_on_out), .reset(turn_off_out));  // open: clk, K
  and and_1 (and_1_out, clock_1_out, ~Interrupt);  // AND_Gate
  and and_2 (and_2_out, clock_2_out, ~Interrupt);  // AND_Gate
  main main_1 (
    .Clk1pulso(and_2_out), .Clk2pulsos(and_1_out), .Reset(j_k_ff_1_qn), .En(j_k_ff_1_q),
    .DataMemRead(ram_1_dout), .Address(main_1_address), .Write(main_1_write), .DataMem(main_1_datamem),
    .ASCIIDATA(main_1_asciidata), .clkTTY(main_1_clktty));  // open: INSTRUCTION
  RAM #(.addrWidth(16), .dataWidth(16)) ram_1 (
    .addr(main_1_address), .we(main_1_write), .oe(not_1_out), .clk(and_2_out), .din(main_1_datamem),
    .dout(ram_1_dout));
  not not_1 (not_1_out, main_1_write);
  TTY #(.rows(32)) tty_1 (.data(main_1_asciidata), .clk(main_1_clktty), .we(main_1_clktty), .clr(j_k_ff_1_qn));
endmodule

module ALU (
  input  [15:0] Data,
  input  [15:0] ACC,
  input  sub,
  input  Enable,
  input  [2:0] Operation,
  input  clk,
  input  RESET,
  output [15:0] out_8,
  output [15:0] S,
  output Zero,
  output [3:0] Flag_out,
  output Sign,
  output greater,
  output overflow,
  output StoreRes
);

  wire and_2_out, and_4_out, comparator_1_gt, comparator_2_eq, not_1_out, not_2_out, not_3_out, or_1_out;
  wire [14:0] adder_2_out;
  wire [15:0] adder_1_out, and_1_out, controlled_buffer_1_out, controlled_buffer_2_out, divider_1_out,
       divider_1_rem, multiplexer_1_out, multiplexer_2_out, multiplier_1_out, or_2_out, subtractor_1_out,
       xor_1_out;

  LED signalSub (.in(sub));
  or or_1 (or_1_out, RESET, not_1_out);
  Counter #(.max('h1), .width(1)) counter_1 (
    .count(Enable), .Q(StoreRes), .clk(clk), .clr(or_1_out));  // open: load, D, carry, up
  not not_1 (not_1_out, Enable);
  Adder #(.width(16)) adder_1 (.a(Data), .b(ACC), .out(adder_1_out), .cin(1'b0), .cout(overflow));
  Divider #(.width(16)) divider_1 (.a(Data), .b(ACC), .out(divider_1_out), .rem(divider_1_rem));  // open: upper
  Subtractor #(.width(16)) subtractor_1 (.a(Data), .b(ACC), .out(subtractor_1_out), .bin(1'b0));  // open: bout
  Multiplier #(.width(16)) multiplier_1 (.a(Data), .b(ACC), .out(multiplier_1_out));  // open: cin, cout
  Multiplexer #(.width(16)) multiplexer_1 (.in0(Data), .in1(ACC), .out(multiplexer_1_out), .sel(sub));
  assign controlled_buffer_1_out = not_3_out ? divider_1_out : 16'bz;  // Controlled_Buffer controlled_buffer_1
  assign and_1_out = Data & ACC;  // AND_Gate and_1, 16 bits wide
  assign xor_1_out = Data ^ ACC;  // XOR_Gate xor_1, 16 bits wide
  assign or_2_out = Data | ACC;  // OR_Gate or_2, 16 bits wide
  Comparator #(.width(16)) comparator_1 (.a(Data), .b(ACC), .gt(comparator_1_gt), .eq(Zero));  // open: lt
  Adder #(.width(16)) adder_2 (.a(Data), .b(ACC), .out({Sign, adder_2_out}), .cin(1'b0));  // open: cout
  Multiplexer #(.width(16)) multiplexer_2 (
    .in0(adder_1_out), .in1(subtractor_1_out), .out(multiplexer_2_out), .sel(sub));
  assign controlled_buffer_2_out = not_3_out ? divider_1_rem : 16'bz;  // Controlled_Buffer controlled_buffer_2
  Multiplexer #(.enable("true"), .select(3), .width(16)) multiplexer_3 (
    .in0(multiplexer_2_out), .in1(multiplier_1_out), .in2(multiplexer_1_out), .in3(controlled_buffer_1_out),
    .in4(and_1_out), .in5(xor_1_out), .in6(or_2_out), .in7(controlled_buffer_2_out), .out(out_8),
    .sel(Operation), .en(Enable));
  not not_2 (not_2_out, Zero);
  Comparator #(.width(16)) comparator_2 (.a(ACC), .b({16{1'b0}}), .eq(comparator_2_eq));  // open: gt, lt
  Register #(.width(16)) register_1 (.D(out_8), .en(and_2_out), .Q(S), .clk(clk), .clr(RESET));
  and and_2 (and_2_out, Enable, ~StoreRes);  // AND_Gate
  and and_3 (greater, comparator_1_gt, not_2_out);
  not not_3 (not_3_out, comparator_2_eq);
  and and_4 (and_4_out, Enable, ~StoreRes);  // AND_Gate
  Register #(.width(4)) FLAGREG (
    .D({overflow, greater, Sign, Zero}), .en(and_4_out), .Q(Flag_out), .clk(clk), .clr(RESET));

  // Other names for the same wires on the sheet: STRRES = StoreRes

  // Notes on the sheet:
  //   verifica se é zero e invalida o resultado da divisão
endmodule

module RegArray (
  input  [15:0] ALUregister,
  input  [15:0] res16bits,
  input  [7:0] Data,
  input  [7:0] Acc_data,
  input  [2:0] Destin_OP,
  input  [2:0] From,
  input  EN,
  input  [1:0] Op,
  input  [3:0] Cond,
  input  PausePC,
  input  RE,
  input  Back,
  input  NextChar,
  input  NCLK2,
  input  Ck,
  input  Nclock,
  input  clk2,
  output [15:0] TO_ALU,
  output AluSignal,
  output Enable_ALU,
  output [2:0] ALU_OP,
  output [15:0] TO_ACC,
  output [15:0] to_memory,
  output [7:0] INSTRUCTION,
  output ALU16bit,
  output [15:0] SP,
  output en_ACC,
  output write,
  output [15:0] ADDRESS_BUS,
  output [15:0] visuAdd,
  output EnableDecoder,
  output [3:0] ASCIIFormat,
  output StoreFormat,
  output Sign
);

  wire A_to_M, acc_imm_en_reg, ALU, and_1_out, and_2_out, and_4_out, and_5_out, and_6_out, and_7_out,
       and_8_out, and_9_out, and_10_out, and_11_out, and_13_out, and_14_out, and_15_out, and_16_out,
       and_19_out, and_20_out, and_21_out, and_22_out, and_23_out, and_24_out, and_25_out, and_26_out,
       and_27_out, and_28_out, and_29_out, and_30_out, and_33_out, and_34_out, and_35_out, and_36_out,
       bc_en_reg, ClockForResult, de_en_reg, demultiplexer_1_out1, demultiplexer_1_out3,
       demultiplexer_1_out4, demultiplexer_1_out5, demultiplexer_3_out0, demultiplexer_3_out1,
       demultiplexer_3_out2, demultiplexer_3_out3, demultiplexer_3_out4, demultiplexer_3_out5,
       demultiplexer_3_out6, demultiplexer_4_out0, demultiplexer_4_out2, demultiplexer_4_out4,
       demultiplexer_5_out0, demultiplexer_5_out1, demultiplexer_6_out0, demultiplexer_6_out1,
       demultiplexer_7_out0, demultiplexer_7_out1, demultiplexer_9_out0, demultiplexer_9_out1,
       demultiplexer_9_out2, demultiplexer_9_out3, demultiplexer_9_out4, demultiplexer_9_out5,
       demultiplexer_9_out6, demultiplexer_9_out7, eax_en_reg, ebx_en_reg, en_stackP, enableEvenALU, EnAcc1,
       end_of_Instruction, EnOutASCII, hl_en_reg, incAddress, j_k_ff_1_q, JMP, JMPOUT, LOADWORD, LXI, MOV,
       MOVP_ACC_enable, MOVP_BC, MOVP_DE, MOVP_eax_enable, MOVP_ebx_enable, MOVP_enable, MOVP_HL,
       MOVP_SP_enable, MOVP_WZ, multiplexer_7_out, multiplexer_14_out, multiplexer_15_out,
       multiplexer_16_out, mva, not_2_out, not_3_out, not_4_out, not_5_out, not_6_out, not_7_out, not_8_out,
       not_9_out, not_10_out, not_11_out, not_13_out, not_write, o_data, or_1_out, or_3_out, or_4_out,
       or_5_out, or_7_out, or_8_out, or_10_out, or_11_out, or_12_out, or_13_out, or_14_out, or_15_out,
       or_16_out, or_17_out, or_18_out, or_19_out, or_20_out, or_22_out, or_23_out, or_24_out, or_25_out,
       or_26_out, or_27_out, or_28_out, or_29_out, or_32_out, or_34_out, pairs, PAIRSELECTOR_q, rclk,
       READDATA, READenable, readOPbits, ReturnOut, st16, sta, stck_en_reg, W, wr, write16, wz_en_reg, Z, zAc;
  wire [2:0] controlled_buffer_2_out, LD_op, multiplexer_4_out, multiplexer_6_out, multiplexer_9_out,
       multiplexer_10_out;
  wire [3:0] bit_extender_1_out;
  wire [7:0] b_reg_data, c_reg_data, controlled_buffer_1_out, highpairselected_data, lowpairselected_data,
       multiplexer_5_out, multiplexer_8_out, multiplexer_13_out, multiplexer_17_out, multiplexer_18_out,
       multiplexer_19_out, multiplexer_22_out;
  wire [7:3] DATALOADED_q;
  wire [15:0] adder_1_out, adder_2_out, bit_extender_2_out, bit_extender_3_out, bit_extender_4_out,
       controlled_buffer_3_out, controlled_buffer_4_out, Eax_data, eax_reg_data, Ebx_data, ebx_reg_data,
       MOVP_data_selected, multiplexer_11_out, multiplexer_12_out, multiplexer_23_out, multiplexer_24_out,
       multiplexer_25_out, multiplexer_26_out, multiplexer_28_out, multiplexer_29_out, multiplexer_30_out,
       multiplexer_35_out, PairBCdata, PairDEdata, PairHLdata, PairWZdata, pc_1_q;

  and and_1 (and_1_out, ~From[0], From[1], From[2]);  // AND_Gate
  and and_2 (and_2_out, ~Destin_OP[0], Destin_OP[1], Destin_OP[2], Op[0], ~Op[1]);  // AND_Gate
  and and_3 (not_write, and_1_out, and_2_out);
  and and_4 (and_4_out, NCLK2, ~ALU16bit, Nclock);  // AND_Gate
  and and_5 (and_5_out, Destin_OP[0], ~Destin_OP[1], Destin_OP[2], ~Op[0], ~Op[1]);  // AND_Gate
  not not_1 (end_of_Instruction, and_4_out);
  and and_6 (and_6_out, Destin_OP[0], ~Destin_OP[1], ~Destin_OP[2], ~Op[0], ~Op[1]);  // AND_Gate
  Multiplexer #(.width(3)) multiplexer_1 (.in0(Destin_OP), .in1(3'b000), .out(INSTRUCTION[5:3]), .sel(readOPbits));
  Multiplexer #(.width(2)) multiplexer_2 (.in0(Op), .in1(2'b00), .out(INSTRUCTION[7:6]), .sel(readOPbits));
  and and_7 (and_7_out, ~and_6_out, ~and_5_out, LXI);  // AND_Gate
  Demultiplexer #(.enable("true"), .select(3)) demultiplexer_1 (
    .out0(EnAcc1), .out1(demultiplexer_1_out1), .out2(EnOutASCII), .out3(demultiplexer_1_out3),
    .out4(demultiplexer_1_out4), .out5(demultiplexer_1_out5), .out6(A_to_M), .out7(o_data), .in(EN),
    .sel(INSTRUCTION[2:0]), .en(or_1_out));
  or or_1 (or_1_out, and_7_out, JMP);
  or or_2 (readOPbits, READenable, EnableDecoder);
  and and_8 (and_8_out, enableEvenALU, ALU);
  not not_2 (not_2_out, READenable);
  not not_3 (not_3_out, EnOutASCII);
  Multiplexer #(.width(3)) multiplexer_3 (.in0(From), .in1(3'b000), .out(INSTRUCTION[2:0]), .sel(readOPbits));
  Multiplexer #(.width(3)) multiplexer_4 (
    .in0(multiplexer_6_out), .in1(INSTRUCTION[2:0]), .out(multiplexer_4_out), .sel(sta));
  and and_9 (and_9_out, LXI, not_2_out, not_3_out);
  and and_10 (and_10_out, Destin_OP[0], ~Destin_OP[1], Destin_OP[2], ~Op[0], ~Op[1]);  // AND_Gate
  and and_11 (and_11_out, EnOutASCII, Ck);
  or or_3 (or_3_out, Back, RE);
  assign controlled_buffer_1_out = sta ? Acc_data : 8'bz;  // Controlled_Buffer controlled_buffer_1
  Demultiplexer #(.select(2)) demultiplexer_2 (
    .out0(LXI), .out1(MOV), .out2(ALU), .out3(JMP), .in(EN), .sel(INSTRUCTION[7:6]));
  not not_4 (not_4_out, Cond[0]);
  not not_5 (not_5_out, Cond[1]);
  not not_6 (not_6_out, Cond[2]);
  not not_7 (not_7_out, Cond[3]);
  J_K_Flip_Flop DECODERREGSTATE (
    .J(and_11_out), .Q(EnableDecoder), .preset(and_11_out), .reset(or_3_out));  // open: clk, K, Qn
  Multiplexer #(.width(8)) multiplexer_5 (
    .in0(multiplexer_22_out), .in1(controlled_buffer_1_out), .out(multiplexer_5_out), .sel(sta));
  or or_4 (or_4_out, and_8_out, ALU);
  or or_5 (or_5_out, ALU, sta, MOV);
  Demultiplexer #(.select(3)) demultiplexer_3 (
    .out0(demultiplexer_3_out0), .out1(demultiplexer_3_out1), .out2(demultiplexer_3_out2),
    .out3(demultiplexer_3_out3), .out4(demultiplexer_3_out4), .out5(demultiplexer_3_out5),
    .out6(demultiplexer_3_out6), .out7(zAc), .in(or_5_out), .sel(multiplexer_4_out));
  Demultiplexer #(.select(3)) demultiplexer_4 (
    .out0(demultiplexer_4_out0), .out1(sta), .out2(demultiplexer_4_out2), .out3(st16),
    .out4(demultiplexer_4_out4), .out5(ALU16bit), .out6(en_stackP), .out7(write16), .in(and_9_out),
    .sel(INSTRUCTION[5:3]));
  Multiplexer #(.width(3)) multiplexer_6 (
    .in0(INSTRUCTION[5:3]), .in1(INSTRUCTION[2:0]), .out(multiplexer_6_out), .sel(ALU));
  or or_6 (enableEvenALU, EnAcc1, and_10_out);
  and and_12 (LOADWORD, JMP, demultiplexer_1_out1);
  not not_8 (not_8_out, LXI);
  Multiplexer #(.enable("true"), .select(3)) multiplexer_7 (
    .in0(Cond[0]), .in1(not_4_out), .in2(Cond[1]), .in3(not_5_out), .in4(Cond[2]), .in5(not_6_out),
    .in6(Cond[3]), .in7(not_7_out), .out(multiplexer_7_out), .sel(INSTRUCTION[5:3]), .en(JMP));
  or or_7 (or_7_out, JMP, ALU);
  Counter #(.max('h1), .width(1)) PAIRSELECTOR (
    .count(LXI), .Q(PAIRSELECTOR_q), .clk(Ck), .clr(or_8_out));  // open: load, D, carry, up
  or or_8 (or_8_out, not_8_out, EnAcc1, not_9_out, RE);
  or or_9 (pairs, en_stackP, demultiplexer_4_out4, demultiplexer_4_out2, demultiplexer_4_out0);
  Demultiplexer #(.enable("true")) demultiplexer_5 (
    .out0(demultiplexer_5_out0), .out1(demultiplexer_5_out1), .in(demultiplexer_4_out0),
    .sel(PAIRSELECTOR_q), .en(demultiplexer_4_out0));
  Demultiplexer #(.enable("true")) demultiplexer_6 (
    .out0(demultiplexer_6_out0), .out1(demultiplexer_6_out1), .in(demultiplexer_4_out2),
    .sel(PAIRSELECTOR_q), .en(demultiplexer_4_out2));
  Demultiplexer #(.enable("true")) demultiplexer_7 (
    .out0(demultiplexer_7_out0), .out1(demultiplexer_7_out1), .in(demultiplexer_4_out4),
    .sel(PAIRSELECTOR_q), .en(demultiplexer_4_out4));
  Demultiplexer #(.enable("true")) demultiplexer_8 (
    .out0(W), .out1(Z), .in(en_stackP), .sel(PAIRSELECTOR_q), .en(en_stackP));
  not not_9 (not_9_out, pairs);
  or or_10 (or_10_out, demultiplexer_1_out3, multiplexer_7_out);
  and and_13 (and_13_out, or_10_out, JMP);
  Bit_Extender #(.out_width(4)) bit_extender_1 (.in(Data), .out(bit_extender_1_out));
  not not_10 (not_10_out, EnableDecoder);
  not not_11 (not_11_out, EnableDecoder);
  Multiplexer #(.select(3), .width(8)) multiplexer_8 (
    .in0(multiplexer_22_out), .in1(multiplexer_5_out), .in2(multiplexer_22_out), .in3(multiplexer_22_out),
    .in4(multiplexer_22_out), .in5(multiplexer_22_out), .in6(Data), .in7(multiplexer_22_out),
    .out(multiplexer_8_out), .sel(multiplexer_10_out));
  Multiplexer #(.width(3)) multiplexer_9 (
    .in0(INSTRUCTION[2:0]), .in1(INSTRUCTION[5:3]), .out(multiplexer_9_out), .sel(sta));
  not not_12 (incAddress, LOADWORD);
  or or_11 (or_11_out, StoreFormat, not_10_out);
  or or_12 (or_12_out, StoreFormat, not_11_out);
  Multiplexer #(.width(3)) multiplexer_10 (
    .in0(multiplexer_9_out), .in1(INSTRUCTION[5:3]), .out(multiplexer_10_out), .sel(o_data));
  not not_13 (not_13_out, Ck);
  Register #(.width(4)) ASCIIREG (
    .D(bit_extender_1_out), .en(or_11_out), .Q(ASCIIFormat), .clk(ClockForResult), .clr(or_3_out));
  Register #(.width(1)) SIGNREG (.D(Data[7]), .en(or_12_out), .Q(Sign), .clk(ClockForResult), .clr(or_3_out));
  assign controlled_buffer_2_out = or_7_out ? INSTRUCTION[5:3] : 3'bz;  // Controlled_Buffer controlled_buffer_2
  or or_13 (or_13_out, demultiplexer_3_out6, wz_en_reg, W);
  or or_14 (or_14_out, demultiplexer_3_out0, bc_en_reg, ALU16bit, demultiplexer_5_out0);
  or or_15 (or_15_out, demultiplexer_3_out1, bc_en_reg, ALU16bit, demultiplexer_5_out1);
  or or_16 (or_16_out, demultiplexer_3_out2, de_en_reg, demultiplexer_6_out0);
  or or_17 (or_17_out, demultiplexer_3_out3, de_en_reg, demultiplexer_6_out1);
  or or_18 (or_18_out, demultiplexer_3_out4, hl_en_reg, demultiplexer_7_out0);
  or or_19 (or_19_out, demultiplexer_3_out5, hl_en_reg, demultiplexer_7_out1);
  or or_20 (or_20_out, Back, and_13_out);
  Multiplexer #(.width(16)) multiplexer_11 (.in0(SP), .in1(visuAdd), .out(multiplexer_11_out), .sel(Back));
  or or_21 (mva, zAc, wz_en_reg, Z);
  and and_14 (and_14_out, end_of_Instruction, or_14_out);
  and and_15 (and_15_out, end_of_Instruction, or_15_out);
  Multiplexer #(.width(16)) multiplexer_12 (
    .in0(multiplexer_11_out), .in1(SP), .out(multiplexer_12_out), .sel(ReturnOut));
  Multiplexer #(.width(8)) multiplexer_13 (
    .in0(multiplexer_8_out), .in1(res16bits[7:0]), .out(multiplexer_13_out), .sel(ALU16bit));
  and and_16 (and_16_out, or_13_out, ~not_write);  // AND_Gate
  Multiplexer multiplexer_14 (.in0(and_14_out), .in1(1'b0), .out(multiplexer_14_out), .sel(en_stackP));
  Multiplexer multiplexer_15 (.in0(and_15_out), .in1(1'b0), .out(multiplexer_15_out), .sel(en_stackP));
  Multiplexer multiplexer_16 (.in0(rclk), .in1(ClockForResult), .out(multiplexer_16_out), .sel(ALU16bit));
  or or_22 (or_22_out, StoreFormat, or_20_out);
  Multiplexer #(.width(8)) multiplexer_17 (
    .in0(multiplexer_8_out), .in1(res16bits[15:8]), .out(multiplexer_17_out), .sel(ALU16bit));
  Register u_W (.D(b_reg_data), .en(or_13_out), .Q(PairWZdata[15:8]), .clk(rclk), .clr(RE));
  Register B (.D(b_reg_data), .en(multiplexer_14_out), .Q(PairBCdata[15:8]), .clk(multiplexer_16_out), .clr(RE));
  Register D (.D(b_reg_data), .en(or_16_out), .Q(PairDEdata[15:8]), .clk(rclk), .clr(RE));
  Register H (.D(b_reg_data), .en(or_18_out), .Q(PairHLdata[15:8]), .clk(rclk), .clr(RE));
  Multiplexer #(.width(8)) multiplexer_18 (
    .in0(multiplexer_17_out), .in1({Op, Destin_OP, From}), .out(multiplexer_18_out), .sel(READenable));
  Multiplexer #(.width(8)) multiplexer_19 (
    .in0(multiplexer_13_out), .in1(Data), .out(multiplexer_19_out), .sel(READenable));
  Register C (.D(c_reg_data), .en(multiplexer_15_out), .Q(PairBCdata[7:0]), .clk(multiplexer_16_out), .clr(RE));
  Register E (.D(c_reg_data), .en(or_17_out), .Q(PairDEdata[7:0]), .clk(rclk), .clr(RE));
  Register L (.D(c_reg_data), .en(or_19_out), .Q(PairHLdata[7:0]), .clk(rclk), .clr(RE));
  and and_17 (JMPOUT, EnableDecoder, clk2, Ck);
  and and_18 (ReturnOut, Back, Nclock, Ck);
  Multiplexer #(.width(8)) multiplexer_20 (
    .in0(multiplexer_18_out), .in1(highpairselected_data), .out(b_reg_data), .sel(MOVP_enable));
  Multiplexer #(.width(8)) multiplexer_21 (
    .in0(multiplexer_19_out), .in1(lowpairselected_data), .out(c_reg_data), .sel(MOVP_enable));
  Register u_Z (.D(c_reg_data), .en(mva), .Q(PairWZdata[7:0]), .clk(rclk), .clr(RE));
  and and_19 (and_19_out, EnAcc1, MOVP_eax_enable);
  PC pc_1 (
    .Load(or_22_out), .Pause(PausePC), .ADDRESS(multiplexer_12_out), .Clock(not_13_out), .enable(EN),
    .Reset(RE), .Q(pc_1_q));
  and and_20 (and_20_out, ~clk2, ~Ck);  // AND_Gate
  Multiplexer #(.select(3), .width(8)) multiplexer_22 (
    .in0(PairBCdata[15:8]), .in1(PairBCdata[7:0]), .in2(PairDEdata[15:8]), .in3(PairDEdata[7:0]),
    .in4(PairHLdata[7:0]), .in5(PairHLdata[15:8]), .in6(PairWZdata[15:8]), .in7(PairWZdata[7:0]),
    .out(multiplexer_22_out), .sel(INSTRUCTION[2:0]));
  and and_21 (and_21_out, st16, ~MOVP_enable, and_19_out);  // AND_Gate
  and and_22 (and_22_out, EnAcc1, MOVP_ebx_enable);
  J_K_Flip_Flop JMPSTATEOUT (
    .J(EnableDecoder), .Q(StoreFormat), .preset(EnableDecoder), .reset(or_23_out));  // open: clk, K, Qn
  or or_23 (or_23_out, and_20_out, j_k_ff_1_q);
  and and_23 (and_23_out, ~EnableDecoder, ~Back);  // AND_Gate
  or or_24 (or_24_out, and_21_out, eax_en_reg);
  and and_24 (and_24_out, st16, ~MOVP_enable, and_22_out);  // AND_Gate
  Multiplexer #(.width(16)) multiplexer_23 (
    .in0(PairWZdata), .in1({Op, Destin_OP, From, Data}), .out(multiplexer_23_out), .sel(READenable));
  or or_25 (or_25_out, StoreFormat, and_23_out);
  not not_14 (ClockForResult, Ck);
  or or_26 (or_26_out, and_24_out, ebx_en_reg);
  and and_25 (and_25_out, A_to_M, sta);
  Multiplexer #(.width(16)) multiplexer_24 (
    .in0(multiplexer_23_out), .in1({highpairselected_data, lowpairselected_data}), .out(multiplexer_24_out),
    .sel(MOVP_SP_enable));
  or or_27 (or_27_out, en_stackP, MOVP_SP_enable, stck_en_reg);
  Register #(.width(16)) REGG (.D(ebx_reg_data), .en(or_26_out), .Q(Ebx_data), .clk(ClockForResult), .clr(RE));
  Register #(.width(16)) Address_reg (
    .D(multiplexer_26_out), .en(or_25_out), .Q(visuAdd), .clk(ClockForResult), .clr(RE));
  and and_26 (and_26_out, StoreFormat, ~clk2, ~Ck);  // AND_Gate
  or or_28 (or_28_out, Back, RE);
  or or_29 (or_29_out, MOV, and_25_out);
  Register #(.width(16)) StackPointer (.D(multiplexer_24_out), .en(or_27_out), .Q(SP), .clk(ClockForResult), .clr(RE));
  Register #(.width(16)) REGF (.D(eax_reg_data), .en(or_24_out), .Q(Eax_data), .clk(ClockForResult), .clr(RE));
  J_K_Flip_Flop j_k_ff_1 (.J(and_26_out), .Q(j_k_ff_1_q), .preset(and_26_out), .reset(or_28_out));  // open: clk, K, Qn
  and and_27 (and_27_out, write16, A_to_M);
  and and_28 (and_28_out, and_16_out, or_29_out);
  assign controlled_buffer_3_out = incAddress ? pc_1_q : 16'bz;  // Controlled_Buffer controlled_buffer_3
  or or_30 (wr, and_27_out, and_28_out);
  Adder #(.width(16)) adder_1 (.a(visuAdd), .b(16'h1), .out(adder_1_out));  // open: cin, cout
  and and_29 (and_29_out, ALU16bit, enableEvenALU);
  Adder #(.width(16)) adder_2 (.a(controlled_buffer_3_out), .b(16'h1), .out(adder_2_out));  // open: cin, cout
  Multiplexer #(.width(16)) multiplexer_25 (
    .in0(pc_1_q), .in1(controlled_buffer_4_out), .out(multiplexer_25_out), .sel(write));
  assign controlled_buffer_4_out = write ? SP : 16'bz;  // Controlled_Buffer controlled_buffer_4
  or or_31 (Enable_ALU, and_29_out, or_4_out);
  Multiplexer #(.width(16)) multiplexer_26 (
    .in0(adder_2_out), .in1(adder_1_out), .out(multiplexer_26_out), .sel(StoreFormat));
  assign bit_extender_2_out = {{8{1'b0}}, multiplexer_22_out};  // Bit_Extender bit_extender_2
  Multiplexer multiplexer_27 (.in0(Ck), .in1(NCLK2), .out(rclk), .sel(READenable));
  Multiplexer #(.width(16)) multiplexer_28 (
    .in0({16{1'b0}}), .in1(bit_extender_2_out), .out(multiplexer_28_out), .sel(Enable_ALU));
  assign bit_extender_3_out = {{8{1'b0}}, PairWZdata[7:0]};  // Bit_Extender bit_extender_3
  assign bit_extender_4_out = {{8{1'b0}}, PairWZdata[15:8]};  // Bit_Extender bit_extender_4
  Multiplexer #(.select(3), .width(16)) multiplexer_29 (
    .in0(PairBCdata), .in1(PairDEdata), .in2(PairHLdata), .in3(PairWZdata), .in4(Eax_data), .in5(Ebx_data),
    .in6(res16bits), .in7(ALUregister), .out(multiplexer_29_out), .sel(Data[2:0]));
  Multiplexer #(.enable("true"), .select(2), .width(16)) multiplexer_30 (
    .in0(PairBCdata), .in1(PairDEdata), .in2(PairHLdata), .in3(PairWZdata), .out(multiplexer_30_out),
    .sel(Data[1:0]), .en(st16));
  or or_32 (or_32_out, write16, wr);
  Multiplexer #(.width(16)) multiplexer_31 (.in0(multiplexer_28_out), .in1(Ebx_data), .out(TO_ALU), .sel(ALU16bit));
  Multiplexer #(.width(3)) multiplexer_32 (
    .in0(controlled_buffer_2_out), .in1(INSTRUCTION[2:0]), .out(ALU_OP), .sel(ALU16bit));
  Multiplexer #(.width(16)) multiplexer_33 (
    .in0(bit_extender_4_out), .in1(multiplexer_29_out), .out(to_memory), .sel(and_30_out));
  and and_30 (and_30_out, write16, A_to_M);
  and and_31 (write, or_32_out, Ck);
  Multiplexer #(.width(16)) multiplexer_34 (.in0(multiplexer_25_out), .in1(SP), .out(ADDRESS_BUS), .sel(READenable));
  Multiplexer #(.width(16)) multiplexer_35 (
    .in0(bit_extender_3_out), .in1(Eax_data), .out(multiplexer_35_out), .sel(ALU16bit));
  Multiplexer #(.width(16)) multiplexer_36 (
    .in0(multiplexer_30_out), .in1(MOVP_data_selected), .out({highpairselected_data, lowpairselected_data}),
    .sel(MOVP_enable));
  and and_32 (READDATA, LOADWORD, NCLK2);
  Multiplexer #(.width(16)) multiplexer_37 (
    .in0(multiplexer_35_out), .in1({Op, Destin_OP, From, Data}), .out(TO_ACC), .sel(READenable));
  and and_33 (and_33_out, mva, MOV, clk2);
  Multiplexer #(.width(16)) multiplexer_38 (
    .in0({highpairselected_data, lowpairselected_data}), .in1({Op, Destin_OP, From, Data}),
    .out(ebx_reg_data), .sel(READenable));
  Multiplexer #(.width(16)) multiplexer_39 (
    .in0({highpairselected_data, lowpairselected_data}), .in1({Op, Destin_OP, From, Data}),
    .out(eax_reg_data), .sel(READenable));
  or or_33 (en_ACC, and_33_out, ALU16bit, acc_imm_en_reg);
  and and_34 (and_34_out, NCLK2, Nclock, READenable);
  or or_34 (or_34_out, RE, and_34_out);
  J_K_Flip_Flop j_k_ff_2 (.J(READDATA), .Q(READenable), .preset(READDATA), .reset(or_34_out));  // open: clk, K, Qn
  Register IR (.D(INSTRUCTION), .en(EN), .clk(NCLK2), .clr(RE));  // open: Q
  Register DATALOADED (.D(Data), .en(EN), .Q({DATALOADED_q, LD_op}), .clk(clk2), .clr(RE));
  and and_35 (and_35_out, ~From[0], ~From[1], ~From[2]);  // AND_Gate
  and and_36 (and_36_out, Destin_OP[0], Destin_OP[1], ~Destin_OP[2], ~Op[0], ~Op[1]);  // AND_Gate
  and and_37 (MOVP_enable, and_35_out, and_36_out);
  Demultiplexer #(.select(3)) demultiplexer_9 (
    .out0(demultiplexer_9_out0), .out1(demultiplexer_9_out1), .out2(demultiplexer_9_out2),
    .out3(demultiplexer_9_out3), .out4(demultiplexer_9_out4), .out5(demultiplexer_9_out5),
    .out6(demultiplexer_9_out6), .out7(demultiplexer_9_out7), .in(READenable), .sel(LD_op));
  Demultiplexer #(.select(3)) demultiplexer_10 (
    .out0(MOVP_BC), .out1(MOVP_DE), .out2(MOVP_HL), .out3(MOVP_WZ), .out4(MOVP_eax_enable),
    .out5(MOVP_ebx_enable), .out6(MOVP_ACC_enable), .out7(MOVP_SP_enable), .in(MOVP_enable), .sel(Data[5:3]));
  or or_35 (bc_en_reg, MOVP_BC, demultiplexer_9_out0);
  or or_36 (de_en_reg, MOVP_DE, demultiplexer_9_out1);
  or or_37 (hl_en_reg, MOVP_HL, demultiplexer_9_out2);
  or or_38 (wz_en_reg, MOVP_WZ, demultiplexer_9_out3);
  or or_39 (eax_en_reg, MOVP_eax_enable, demultiplexer_9_out4);
  or or_40 (ebx_en_reg, MOVP_ebx_enable, demultiplexer_9_out5);
  or or_41 (acc_imm_en_reg, MOVP_ACC_enable, demultiplexer_9_out6);
  or or_42 (stck_en_reg, MOVP_SP_enable, demultiplexer_9_out7);
  Multiplexer #(.select(3), .width(16)) multiplexer_40 (
    .in0(PairBCdata), .in1(PairDEdata), .in2(PairHLdata), .in3(PairWZdata), .in4(Eax_data), .in5(Ebx_data),
    .in6(res16bits), .in7(SP), .out(MOVP_data_selected), .sel(Data[2:0]));

  assign AluSignal = Data[7];

  // Other names for the same wires on the sheet: Addr[15:0] = visuAdd; ADDRESSTOLOAD[15:0] = SP; ALU16 = ALU16bit;
  //   ALUreg[15:0] = ALUregister; ACCVALUE[15:0] = res16bits; AluResult[15:0] = res16bits;
  //   AluResultHigh[7:0] = res16bits[15:8]; AluResultLow[7:0] = res16bits[7:0]; ALU16op[2:0] = INSTRUCTION[2:0];
  //   ASCIIDATA[15:0] = {INSTRUCTION, Data}; trheeBits2[2:0] = INSTRUCTION[2:0]; trheeBits1[2:0] = INSTRUCTION[5:3];
  //   twoBits[1:0] = INSTRUCTION[7:6]; ClockReg = Ck; EnAcc2 = EnAcc1; JMPONLY = StoreFormat;
  //   MOVP_Instruction = MOVP_enable; Nck = Nclock;
  //   pairselected_data[15:0] = {highpairselected_data, lowpairselected_data}; RESET = RE;
  //   StopStoringAddress = EnableDecoder; d_reg_data[7:0] = b_reg_data; h_reg_data[7:0] = b_reg_data;
  //   w_reg_data[7:0] = b_reg_data; MOVP_op_Select[2:0] = Data[2:0]; op16[1:0] = Data[1:0]; STW_op[2:0] = Data[2:0];
  //   word_data[15:0] = {Op, Destin_OP, From, Data}; MOVP_op[2:0] = Data[5:3]; d1[2:0] = From;
  //   word[7:0] = {Op, Destin_OP, From}; d2[2:0] = Destin_OP; d3[1:0] = Op; WRITEDATA = write;
  //   e_reg_data[7:0] = c_reg_data; l_reg_data[7:0] = c_reg_data; z_reg_data[7:0] = c_reg_data
endmodule

module DEC (
  input  [15:0] in_1,
  output [7:0] DATA,
  output [2:0] FROM,
  output [2:0] DESTINY,
  output [1:0] OP
);


  assign DATA = in_1[7:0];
  assign DESTINY = in_1[13:11];
  assign FROM = in_1[10:8];
  assign OP = in_1[15:14];
endmodule

module plus3 (
  input  A3,
  input  A2,
  input  A1,
  input  A0,
  output Q3,
  output Q2,
  output Q1,
  output Q0
);

  wire adder_1_cout, and_1_out, and_2_out, and_3_out, not_1_out, or_1_out, or_2_out, xor_3_out;

  or or_1 (or_1_out, A1, A0);
  and and_1 (and_1_out, A2, or_1_out);
  or or_2 (or_2_out, A3, and_1_out);
  xor xor_1 (Q0, or_2_out, A0);
  and and_2 (and_2_out, or_2_out, Q0);
  not not_1 (not_1_out, A1);
  and and_3 (and_3_out, not_1_out, and_2_out);
  xor xor_2 (Q1, and_2_out, A1);
  xor xor_3 (xor_3_out, or_2_out, and_3_out);
  Adder #(.width(1)) adder_1 (.a(A2), .b(xor_3_out), .out(Q2), .cout(adder_1_cout));  // open: cin
  xor xor_4 (Q3, A3, adder_1_cout);
endmodule

module ASCIIDECODER (
  input  [15:0] Data,
  input  Sign,
  input  [3:0] format,
  input  EnableOut,
  input  clk2tiks,
  input  Nclk2tiks,
  input  NormalClock,
  output Back,
  output PausePC,
  output [3:0] D1unit,
  output [3:0] D2Ten,
  output [3:0] D3Hundred,
  output [3:0] D4Thousand,
  output [3:0] D5TenThousand,
  output [6:0] ASCIID,
  output nextChar,
  output ClkToOUT
);

  wire A, and_3_out, and_4_out, and_5_out, and_7_out, and_8_out, and_9_out, and_11_out, and_12_out, B,
       Back_t, bck, C, D, E, isZero, j_k_ff_1_q, j_k_ff_3_q, multiplexer_2_out, multiplexer_3_out,
       multiplexer_8_out, multiplexer_9_out, multiplexer_14_out, multiplexer_17_out, Negative, newLine,
       nextAddress, NextChar_t, not_4_out, not_5_out, not_6_out, not_7_out, not_8_out, not_9_out, or_1_out,
       or_2_out, or_9_out, or_10_out, or_12_out, plus3_1_q0, plus3_1_q1, plus3_1_q2, plus3_1_q3, plus3_2_q0,
       plus3_2_q1, plus3_2_q2, plus3_2_q3, plus3_3_q0, plus3_3_q1, plus3_3_q2, plus3_3_q3, plus3_4_q0,
       plus3_4_q1, plus3_4_q2, plus3_4_q3, plus3_5_q0, plus3_5_q1, plus3_5_q2, plus3_5_q3, plus3_6_q0,
       plus3_6_q1, plus3_6_q2, plus3_6_q3, plus3_7_q0, plus3_7_q1, plus3_7_q2, plus3_7_q3, plus3_8_q0,
       plus3_8_q1, plus3_8_q2, plus3_8_q3, plus3_9_q0, plus3_9_q1, plus3_9_q2, plus3_9_q3, plus3_10_q0,
       plus3_10_q1, plus3_10_q2, plus3_10_q3, plus3_11_q0, plus3_11_q1, plus3_11_q2, plus3_11_q3,
       plus3_12_q0, plus3_12_q1, plus3_12_q2, plus3_12_q3, plus3_13_q0, plus3_13_q1, plus3_13_q2,
       plus3_13_q3, plus3_14_q0, plus3_14_q1, plus3_14_q2, plus3_14_q3, plus3_15_q0, plus3_15_q1,
       plus3_15_q2, plus3_15_q3, plus3_16_q0, plus3_16_q1, plus3_16_q2, plus3_16_q3, plus3_17_q0,
       plus3_17_q1, plus3_17_q2, plus3_17_q3, plus3_18_q0, plus3_18_q1, plus3_18_q2, plus3_18_q3,
       plus3_19_q0, plus3_19_q1, plus3_19_q2, plus3_19_q3, plus3_20_q0, plus3_20_q1, plus3_20_q2,
       plus3_20_q3, plus3_21_q0, plus3_21_q1, plus3_21_q2, plus3_21_q3, plus3_22_q0, plus3_22_q1,
       plus3_22_q2, plus3_23_q0, plus3_23_q1, plus3_23_q2, plus3_23_q3, plus3_24_q0, plus3_24_q1,
       plus3_24_q2, plus3_24_q3, plus3_25_q0, plus3_25_q1, plus3_25_q2, plus3_25_q3, plus3_26_q0,
       plus3_26_q1, plus3_26_q2, plus3_27_q0, plus3_27_q1, plus3_27_q2, plus3_27_q3, plus3_28_q0,
       plus3_28_q1, plus3_28_q2, plus3_28_q3, plus3_29_q0, plus3_29_q1, plus3_29_q2, plus3_29_q3, printZero;
  wire [1:0] counter_1_q;
  wire [2:0] counter_2_q;
  wire [3:0] multiplexer_4_out, multiplexer_5_out, multiplexer_6_out, multiplexer_7_out;
  wire [6:0] bit_extender_1_out, multiplexer_13_out, multiplexer_15_out;
  wire [7:0] multiplexer_10_out, multiplexer_11_out, multiplexer_12_out;
  wire [15:0] adder_1_out, not_1_out;
  wire [15:1] multiplexer_1_out;

  assign not_1_out = ~Data;  // NOT_Gate not_1, 16 bits wide
  Adder #(.width(16)) adder_1 (.a(not_1_out), .b(16'h1), .out(adder_1_out));  // open: cin, cout
  or or_1 (or_1_out, Data[15], Data[14], Data[13], Data[12], Data[11], Data[10], Data[9], Data[8]);
  and and_1 (newLine, format[0], ~format[1], format[2], ~format[3]);  // AND_Gate
  not not_2 (isZero, or_1_out);
  Multiplexer #(.width(16)) multiplexer_1 (
    .in0(Data), .in1(adder_1_out), .out({multiplexer_1_out, D1unit[0]}), .sel(Negative));
  not not_3 (Back_t, or_1_out);
  and and_2 (Negative, Data[15], Sign);
  plus3 plus3_1 (
    .A3(1'b0), .A2(multiplexer_1_out[15]), .A1(multiplexer_1_out[14]), .A0(multiplexer_1_out[13]),
    .Q3(plus3_1_q3), .Q2(plus3_1_q2), .Q1(plus3_1_q1), .Q0(plus3_1_q0));
  or or_2 (or_2_out, Data[7], Data[6], Data[5], Data[4], Data[3], Data[2], Data[1], Data[0]);
  plus3 plus3_2 (
    .A3(plus3_1_q2), .A2(plus3_1_q1), .A1(plus3_1_q0), .A0(multiplexer_1_out[12]), .Q3(plus3_2_q3),
    .Q2(plus3_2_q2), .Q1(plus3_2_q1), .Q0(plus3_2_q0));
  plus3 plus3_3 (
    .A3(plus3_2_q2), .A2(plus3_2_q1), .A1(plus3_2_q0), .A0(multiplexer_1_out[11]), .Q3(plus3_3_q3),
    .Q2(plus3_3_q2), .Q1(plus3_3_q1), .Q0(plus3_3_q0));
  or or_3 (NextChar_t, or_1_out, or_2_out);
  plus3 plus3_4 (
    .A3(1'b0), .A2(plus3_1_q3), .A1(plus3_2_q3), .A0(plus3_3_q3), .Q3(plus3_4_q3), .Q2(plus3_4_q2),
    .Q1(plus3_4_q1), .Q0(plus3_4_q0));
  plus3 plus3_5 (
    .A3(plus3_3_q2), .A2(plus3_3_q1), .A1(plus3_3_q0), .A0(multiplexer_1_out[10]), .Q3(plus3_5_q3),
    .Q2(plus3_5_q2), .Q1(plus3_5_q1), .Q0(plus3_5_q0));
  plus3 plus3_6 (
    .A3(plus3_4_q2), .A2(plus3_4_q1), .A1(plus3_4_q0), .A0(plus3_5_q3), .Q3(plus3_6_q3), .Q2(plus3_6_q2),
    .Q1(plus3_6_q1), .Q0(plus3_6_q0));
  plus3 plus3_7 (
    .A3(plus3_5_q2), .A2(plus3_5_q1), .A1(plus3_5_q0), .A0(multiplexer_1_out[9]), .Q3(plus3_7_q3),
    .Q2(plus3_7_q2), .Q1(plus3_7_q1), .Q0(plus3_7_q0));
  plus3 plus3_8 (
    .A3(plus3_6_q2), .A2(plus3_6_q1), .A1(plus3_6_q0), .A0(plus3_7_q3), .Q3(plus3_8_q3), .Q2(plus3_8_q2),
    .Q1(plus3_8_q1), .Q0(plus3_8_q0));
  plus3 plus3_9 (
    .A3(plus3_7_q2), .A2(plus3_7_q1), .A1(plus3_7_q0), .A0(multiplexer_1_out[8]), .Q3(plus3_9_q3),
    .Q2(plus3_9_q2), .Q1(plus3_9_q1), .Q0(plus3_9_q0));
  plus3 plus3_10 (
    .A3(1'b0), .A2(plus3_4_q3), .A1(plus3_6_q3), .A0(plus3_8_q3), .Q3(plus3_10_q3), .Q2(plus3_10_q2),
    .Q1(plus3_10_q1), .Q0(plus3_10_q0));
  plus3 plus3_11 (
    .A3(plus3_8_q2), .A2(plus3_8_q1), .A1(plus3_8_q0), .A0(plus3_9_q3), .Q3(plus3_11_q3), .Q2(plus3_11_q2),
    .Q1(plus3_11_q1), .Q0(plus3_11_q0));
  plus3 plus3_12 (
    .A3(plus3_9_q2), .A2(plus3_9_q1), .A1(plus3_9_q0), .A0(multiplexer_1_out[7]), .Q3(plus3_12_q3),
    .Q2(plus3_12_q2), .Q1(plus3_12_q1), .Q0(plus3_12_q0));
  plus3 plus3_13 (
    .A3(plus3_10_q2), .A2(plus3_10_q1), .A1(plus3_10_q0), .A0(plus3_11_q3), .Q3(plus3_13_q3),
    .Q2(plus3_13_q2), .Q1(plus3_13_q1), .Q0(plus3_13_q0));
  plus3 plus3_14 (
    .A3(plus3_11_q2), .A2(plus3_11_q1), .A1(plus3_11_q0), .A0(plus3_12_q3), .Q3(plus3_14_q3),
    .Q2(plus3_14_q2), .Q1(plus3_14_q1), .Q0(plus3_14_q0));
  plus3 plus3_15 (
    .A3(plus3_12_q2), .A2(plus3_12_q1), .A1(plus3_12_q0), .A0(multiplexer_1_out[6]), .Q3(plus3_15_q3),
    .Q2(plus3_15_q2), .Q1(plus3_15_q1), .Q0(plus3_15_q0));
  plus3 plus3_16 (
    .A3(plus3_13_q2), .A2(plus3_13_q1), .A1(plus3_13_q0), .A0(plus3_14_q3), .Q3(plus3_16_q3),
    .Q2(plus3_16_q2), .Q1(plus3_16_q1), .Q0(plus3_16_q0));
  plus3 plus3_17 (
    .A3(plus3_14_q2), .A2(plus3_14_q1), .A1(plus3_14_q0), .A0(plus3_15_q3), .Q3(plus3_17_q3),
    .Q2(plus3_17_q2), .Q1(plus3_17_q1), .Q0(plus3_17_q0));
  plus3 plus3_18 (
    .A3(plus3_15_q2), .A2(plus3_15_q1), .A1(plus3_15_q0), .A0(multiplexer_1_out[5]), .Q3(plus3_18_q3),
    .Q2(plus3_18_q2), .Q1(plus3_18_q1), .Q0(plus3_18_q0));
  plus3 plus3_19 (
    .A3(plus3_16_q2), .A2(plus3_16_q1), .A1(plus3_16_q0), .A0(plus3_17_q3), .Q3(plus3_19_q3),
    .Q2(plus3_19_q2), .Q1(plus3_19_q1), .Q0(plus3_19_q0));
  plus3 plus3_20 (
    .A3(plus3_17_q2), .A2(plus3_17_q1), .A1(plus3_17_q0), .A0(plus3_18_q3), .Q3(plus3_20_q3),
    .Q2(plus3_20_q2), .Q1(plus3_20_q1), .Q0(plus3_20_q0));
  plus3 plus3_21 (
    .A3(plus3_18_q2), .A2(plus3_18_q1), .A1(plus3_18_q0), .A0(multiplexer_1_out[4]), .Q3(plus3_21_q3),
    .Q2(plus3_21_q2), .Q1(plus3_21_q1), .Q0(plus3_21_q0));
  plus3 plus3_22 (
    .A3(plus3_10_q3), .A2(plus3_13_q3), .A1(plus3_16_q3), .A0(plus3_19_q3), .Q3(D5TenThousand[2]),
    .Q2(plus3_22_q2), .Q1(plus3_22_q1), .Q0(plus3_22_q0));
  plus3 plus3_23 (
    .A3(plus3_19_q2), .A2(plus3_19_q1), .A1(plus3_19_q0), .A0(plus3_20_q3), .Q3(plus3_23_q3),
    .Q2(plus3_23_q2), .Q1(plus3_23_q1), .Q0(plus3_23_q0));
  plus3 plus3_24 (
    .A3(plus3_20_q2), .A2(plus3_20_q1), .A1(plus3_20_q0), .A0(plus3_21_q3), .Q3(plus3_24_q3),
    .Q2(plus3_24_q2), .Q1(plus3_24_q1), .Q0(plus3_24_q0));
  plus3 plus3_25 (
    .A3(plus3_21_q2), .A2(plus3_21_q1), .A1(plus3_21_q0), .A0(multiplexer_1_out[3]), .Q3(plus3_25_q3),
    .Q2(plus3_25_q2), .Q1(plus3_25_q1), .Q0(plus3_25_q0));
  plus3 plus3_26 (
    .A3(plus3_22_q2), .A2(plus3_22_q1), .A1(plus3_22_q0), .A0(plus3_23_q3), .Q3(D5TenThousand[1]),
    .Q2(plus3_26_q2), .Q1(plus3_26_q1), .Q0(plus3_26_q0));
  plus3 plus3_27 (
    .A3(plus3_23_q2), .A2(plus3_23_q1), .A1(plus3_23_q0), .A0(plus3_24_q3), .Q3(plus3_27_q3),
    .Q2(plus3_27_q2), .Q1(plus3_27_q1), .Q0(plus3_27_q0));
  plus3 plus3_28 (
    .A3(plus3_24_q2), .A2(plus3_24_q1), .A1(plus3_24_q0), .A0(plus3_25_q3), .Q3(plus3_28_q3),
    .Q2(plus3_28_q2), .Q1(plus3_28_q1), .Q0(plus3_28_q0));
  plus3 plus3_29 (
    .A3(plus3_25_q2), .A2(plus3_25_q1), .A1(plus3_25_q0), .A0(multiplexer_1_out[2]), .Q3(plus3_29_q3),
    .Q2(plus3_29_q2), .Q1(plus3_29_q1), .Q0(plus3_29_q0));
  and and_3 (and_3_out, EnableOut, clk2tiks);
  and and_4 (and_4_out, EnableOut, Nclk2tiks);
  plus3 plus3_30 (
    .A3(plus3_26_q2), .A2(plus3_26_q1), .A1(plus3_26_q0), .A0(plus3_27_q3), .Q3(D5TenThousand[0]),
    .Q2(D4Thousand[3]), .Q1(D4Thousand[2]), .Q0(D4Thousand[1]));
  plus3 plus3_31 (
    .A3(plus3_27_q2), .A2(plus3_27_q1), .A1(plus3_27_q0), .A0(plus3_28_q3), .Q3(D4Thousand[0]),
    .Q2(D3Hundred[3]), .Q1(D3Hundred[2]), .Q0(D3Hundred[1]));
  plus3 plus3_32 (
    .A3(plus3_28_q2), .A2(plus3_28_q1), .A1(plus3_28_q0), .A0(plus3_29_q3), .Q3(D3Hundred[0]), .Q2(D2Ten[3]),
    .Q1(D2Ten[2]), .Q0(D2Ten[1]));
  plus3 plus3_33 (
    .A3(plus3_29_q2), .A2(plus3_29_q1), .A1(plus3_29_q0), .A0(multiplexer_1_out[1]), .Q3(D2Ten[0]),
    .Q2(D1unit[3]), .Q1(D1unit[2]), .Q0(D1unit[1]));
  LED DECenabled (.in(EnableOut));
  not not_4 (not_4_out, EnableOut);
  or or_4 (A, 1'b0, D5TenThousand[2], D5TenThousand[1], D5TenThousand[0]);
  Counter #(.max('h3), .width(2)) counter_1 (
    .count(PausePC), .Q(counter_1_q), .clk(and_4_out), .clr(not_4_out));  // open: load, D, carry, up
  or or_5 (B, D4Thousand[3], D4Thousand[2], D4Thousand[1], D4Thousand[0]);
  or or_6 (C, D3Hundred[3], D3Hundred[2], D3Hundred[1], D3Hundred[0]);
  Multiplexer #(.select(2)) multiplexer_2 (
    .in0(A), .in1(B), .in2(C), .in3(D), .out(multiplexer_2_out), .sel(counter_1_q));
  J_K_Flip_Flop j_k_ff_1 (
    .J(multiplexer_2_out), .Q(j_k_ff_1_q), .preset(multiplexer_2_out), .reset(not_4_out));  // open: clk, K, Qn
  or or_7 (D, D2Ten[3], D2Ten[2], D2Ten[1], D2Ten[0]);
  or or_8 (E, D1unit[0], D1unit[1], D1unit[2], D1unit[3]);
  Multiplexer #(.select(3)) multiplexer_3 (
    .in0(1'b0), .in1(1'b0), .in2(1'b0), .in3(1'b0), .in4(1'b0), .in5(E), .in6(1'b0), .in7(1'b0),
    .out(multiplexer_3_out), .sel(counter_2_q));
  Hex_Digit_Display TT (.value({1'b0, D5TenThousand[2:0]}));  // open: dp
  Hex_Digit_Display T (.value(D4Thousand));  // open: dp
  Hex_Digit_Display H (.value(D3Hundred));  // open: dp
  Multiplexer #(.width(4)) multiplexer_4 (.in0(4'b0000), .in1(4'b1101), .out(multiplexer_4_out), .sel(Negative));
  or or_9 (or_9_out, multiplexer_3_out, Negative, j_k_ff_1_q);
  Hex_Digit_Display TN (.value(D2Ten));  // open: dp
  Hex_Digit_Display U (.value(D1unit));  // open: dp
  Multiplexer #(.width(4)) multiplexer_5 (.in0(4'b0011), .in1(4'b0010), .out(multiplexer_5_out), .sel(Negative));
  Multiplexer #(.select(3), .width(4)) multiplexer_6 (
    .in0(multiplexer_4_out), .in1({1'b0, D5TenThousand[2:0]}), .in2(D4Thousand), .in3(D3Hundred),
    .in4(D2Ten), .in5(D1unit), .in6(4'b0000), .out(multiplexer_6_out), .sel(counter_2_q));  // open: in7
  Counter #(.max('h6), .width(3)) counter_2 (
    .count(PausePC), .Q(counter_2_q), .clk(and_4_out), .clr(not_4_out));  // open: load, D, carry, up
  not not_5 (not_5_out, 1'b1);
  Multiplexer #(.select(3), .width(4)) multiplexer_7 (
    .in0(multiplexer_5_out), .in1(4'b0011), .in2(4'b0011), .in3(4'b0011), .in4(4'b0011), .in5(4'b0011),
    .in6(4'b0011), .in7(4'b0011), .out(multiplexer_7_out), .sel(counter_2_q));
  Multiplexer #(.select(3)) multiplexer_8 (
    .in0(not_5_out), .in1(not_5_out), .in2(not_5_out), .in3(not_5_out), .in4(not_5_out), .in5(not_5_out),
    .in6(1'b1), .in7(not_5_out), .out(multiplexer_8_out), .sel(counter_2_q));
  or or_10 (or_10_out, or_9_out, and_5_out);
  and and_5 (and_5_out, printZero, isZero);
  and and_6 (printZero, counter_2_q[0], ~counter_2_q[1], counter_2_q[2]);  // AND_Gate
  Multiplexer multiplexer_9 (.in0(1'b0), .in1(multiplexer_8_out), .out(multiplexer_9_out), .sel(multiplexer_17_out));
  Multiplexer #(.width(8)) multiplexer_10 (.in0(Data[15:8]), .in1(8'ha), .out(multiplexer_10_out), .sel(newLine));
  Multiplexer #(.width(8)) multiplexer_11 (.in0(Data[7:0]), .in1({8{1'b0}}), .out(multiplexer_11_out), .sel(newLine));
  Counter #(.max('h1), .width(1)) counter_3 (
    .count(EnableOut), .Q(nextAddress), .clk(and_3_out), .clr(not_4_out));  // open: load, D, carry, up
  Bit_Extender #(.out_width(7)) bit_extender_1 (.in(multiplexer_12_out), .out(bit_extender_1_out));
  Multiplexer #(.width(8)) multiplexer_12 (
    .in0(multiplexer_10_out), .in1(multiplexer_11_out), .out(multiplexer_12_out), .sel(nextAddress));
  Multiplexer #(.width(7)) multiplexer_13 (
    .in0({7{1'b0}}), .in1({multiplexer_7_out[2:0], multiplexer_6_out}), .out(multiplexer_13_out),
    .sel(or_10_out));
  Multiplexer #(.select(4)) multiplexer_14 (
    .in0(Back_t), .in1(Back_t), .in2(Back_t), .in3(not_5_out), .in4(Back_t), .in5(Back_t), .in6(Back_t),
    .in7(Back_t), .in8(Back_t), .in9(Back_t), .in10(Back_t), .in11(Back_t), .in12(Back_t), .in13(Back_t),
    .in14(Back_t), .in15(Back_t), .out(multiplexer_14_out), .sel(format));
  Multiplexer #(.select(4), .width(7)) multiplexer_15 (
    .in0(bit_extender_1_out), .in1(bit_extender_1_out), .in2(bit_extender_1_out), .in3(multiplexer_13_out),
    .in4(bit_extender_1_out), .in5(bit_extender_1_out), .in6(bit_extender_1_out), .in7(bit_extender_1_out),
    .in8(bit_extender_1_out), .in9(bit_extender_1_out), .in10(bit_extender_1_out), .in11(bit_extender_1_out),
    .in12(bit_extender_1_out), .in13(bit_extender_1_out), .in14(bit_extender_1_out),
    .in15(bit_extender_1_out), .out(multiplexer_15_out), .sel(format));
  not not_6 (not_6_out, 1'b1);
  Multiplexer #(.width(7)) multiplexer_16 (.in0(multiplexer_15_out), .in1({7{1'b0}}), .out(ASCIID), .sel(bck));
  Multiplexer #(.select(4)) multiplexer_17 (
    .in0(not_6_out), .in1(not_6_out), .in2(not_6_out), .in3(1'b1), .in4(not_6_out), .in5(not_6_out),
    .in6(not_6_out), .in7(not_6_out), .in8(not_6_out), .in9(not_6_out), .in10(not_6_out), .in11(not_6_out),
    .in12(not_6_out), .in13(not_6_out), .in14(not_6_out), .in15(not_6_out), .out(multiplexer_17_out),
    .sel(format));
  and and_7 (and_7_out, format[0], format[1], ~format[2], ~format[3]);  // AND_Gate
  or or_11 (bck, multiplexer_14_out, multiplexer_9_out);
  Multiplexer multiplexer_18 (.in0(and_4_out), .in1(and_4_out), .out(ClkToOUT), .sel(not_7_out));
  not not_7 (not_7_out, multiplexer_17_out);
  and and_8 (and_8_out, ~multiplexer_9_out, and_7_out, EnableOut);  // AND_Gate
  or or_12 (or_12_out, multiplexer_9_out, not_8_out);
  not not_8 (not_8_out, EnableOut);
  and and_9 (and_9_out, EnableOut, bck);
  J_K_Flip_Flop j_k_ff_2 (.J(and_8_out), .Q(PausePC), .preset(and_8_out), .reset(or_12_out));  // open: clk, K, Qn
  LED writing (.in(PausePC));
  J_K_Flip_Flop j_k_ff_3 (.J(and_9_out), .Q(j_k_ff_3_q), .preset(and_9_out), .reset(not_9_out));  // open: clk, K, Qn
  and and_10 (nextChar, nextAddress, EnableOut, and_3_out);
  and and_11 (and_11_out, clk2tiks, NormalClock, j_k_ff_3_q);
  J_K_Flip_Flop j_k_ff_4 (.J(and_11_out), .Q(Back), .preset(and_11_out), .reset(and_12_out));  // open: clk, K, Qn
  not not_9 (not_9_out, EnableOut);
  and and_12 (and_12_out, ~clk2tiks, ~NormalClock);  // AND_Gate
  LED disableDECODER (.in(Back));

  assign D5TenThousand[3] = 1'b0;

  // Other names for the same wires on the sheet: DataAscii[7:0] = Data[7:0]; DataAscii1[7:0] = Data[15:8];
  //   DecoderEnabled = EnableOut; WriteNumber = PausePC
endmodule
